# Fritzing sketch RFID_125kHz (saved by Fritzing 0.9.3b)

parts:
  125_kHz_RFID_module1 = RDM6300
  Bauteil1 = RDM6300-ANT
  WeMos_D1_Mini1 = WeMos D1 Mini

nets:
  N1: 125_kHz_RFID_module1.TX, 125_kHz_RFID_module1.GND#66, WeMos_D1_Mini1.D2
  N2: 125_kHz_RFID_module1.RX, WeMos_D1_Mini1.D3
  N3: 125_kHz_RFID_module1.GND#60, WeMos_D1_Mini1.G
  +5V: 125_kHz_RFID_module1.+5V, WeMos_D1_Mini1.5V
  N4: 125_kHz_RFID_module1.ANT1, Bauteil1.ANT1
  N5: 125_kHz_RFID_module1.ANT2, Bauteil1.ANT2

custom parts:
  RDM6300: 125 kHz RFID module (serial interface)
  RDM6300-ANT: Antenna

// code stored in the sketch: RFID_125kHz_D1mini.ino
#include "rdm630.h"

#define CO2_TX D2
#define CO2_RX D3

rdm630 rfid(CO2_TX, CO2_RX);  //TX-pin of RDM630 connected to Arduino pin 6

void setup()
{
    Serial.begin(9600);  // start serial to PC
    rfid.begin();
}

void loop()
{
    byte data[6];
    byte length;

    if(rfid.available()){
        rfid.getData(data,length);

        // Die RFID besteht aus den Bytes 1 bis 4 im Daten Array von 0 bis 5
        unsigned long result = 
          ((unsigned long int)data[1]<<24) + 
          ((unsigned long int)data[2]<<16) + 
          ((unsigned long int)data[3]<<8) + 
          data[4];              
        Serial.print("Karten-ID: ");
        Serial.println(result);
    }
}
